// Logisim project part1.circ as structural Verilog: 4 circuits, main circuit main
module main (
  input  s,
  input  x,
  input  y,
  output f
);

  wire n7404_1_p3, n7408_1_p3, n7408_1_p6;

  // _7404 7404_1: pin names not known; wires that end beside it: s, s, n7404_1_p3, 1'b0, 1'b1
  // _7408 7408_1: pin names not known; wires that end beside it: n7404_1_p3, x, n7408_1_p3, s, y, n7408_1_p6, 1'b0, 1'b1
  // _7432 7432_1: pin names not known; wires that end beside it: n7408_1_p3, n7408_1_p6, f, 1'b0, 1'b1, f
endmodule

module part_2 (
  input  a,
  input  b,
  input  c,
  input  d,
  output f
);

  wire n7404_1_p2, n7404_1_p4, n7408_1_p2, n7408_1_p6, n7432_1_p1;

  // _7404 7404_1: pin names not known; wires that end beside it: a, n7404_1_p2, b, n7404_1_p4, 1'b1
  // _7408 7408_1: pin names not known; wires that end beside it: c, n7408_1_p2, 1'b0, n7408_1_p2, n7404_1_p2, n7408_1_p6, n7404_1_p4, d, 1'b1
  // _7432 7432_1: pin names not known; wires that end beside it: n7432_1_p1, n7408_1_p6, f, 1'b0, n7432_1_p1, 1'b0, 1'b1
endmodule

module part_3 (
  input  x,
  input  s,
  input  y,
  output f
);

  wire and_1_out, and_2_out, not_1_out;

  not not_1 (not_1_out, s);
  and and_1 (and_1_out, x, not_1_out);
  and and_2 (and_2_out, s, y);
  or or_1 (f, and_1_out, and_2_out);
endmodule

module part_4 (
  input  c,
  input  a,
  input  b,
  input  d,
  output f
);

  wire and_1_out, and_2_out, and_3_out, and_4_out, and_5_out, and_6_out, not_1_out, not_2_out, not_3_out,
       not_4_out, not_5_out, or_1_out, or_2_out;

  not not_1 (not_1_out, b);
  not not_2 (not_2_out, c);
  not not_3 (not_3_out, a);
  and and_1 (and_1_out, d, not_1_out);
  and and_2 (and_2_out, b, not_2_out);
  and and_3 (and_3_out, not_2_out, not_3_out);
  and and_4 (and_4_out, a, d);
  or or_1 (or_1_out, and_1_out, and_2_out);
  not not_4 (not_4_out, a);
  not not_5 (not_5_out, b);
  or or_2 (or_2_out, and_3_out, and_4_out);
  and and_5 (and_5_out, or_1_out, not_4_out);
  and and_6 (and_6_out, not_5_out, or_2_out);
  or or_3 (f, and_5_out, and_6_out);
endmodule
