// Logisim project part4.circ as structural Verilog: 1 circuit, main circuit main
module main (
  input  c,
  input  a,
  input  b,
  input  d,
  output f
);

  wire and_1_out, and_2_out, and_3_out, and_4_out, and_5_out, and_6_out, not_1_out, not_2_out, not_3_out,
       not_4_out, not_5_out, or_1_out, or_2_out;

  not not_1 (not_1_out, b);
  not not_2 (not_2_out, c);
  not not_3 (not_3_out, a);
  and and_1 (and_1_out, d, not_1_out);
  and and_2 (and_2_out, b, not_2_out);
  and and_3 (and_3_out, not_2_out, not_3_out);
  and and_4 (and_4_out, a, d);
  or or_1 (or_1_out, and_1_out, and_2_out);
  not not_4 (not_4_out, a);
  not not_5 (not_5_out, b);
  or or_2 (or_2_out, and_3_out, and_4_out);
  and and_5 (and_5_out, or_1_out, not_4_out);
  and and_6 (and_6_out, not_5_out, or_2_out);
  or or_3 (f, and_5_out, and_6_out);
endmodule
